// Logisim project Parcial_1_reset_corregido.circ as structural Verilog: 3 circuits, main circuit main
module Moore (
  input  SEL15,
  input  SEL25,
  input  COMPLETE,
  input  CLK,
  input  Reset,
  output MODE15,
  output MODE25,
  output IMPRIME15,
  output IMPRIME25,
  output C2,
  output C1,
  output C0
);

  wire DC0, DC1, DC2, nC0, nC1, nC2, nCOMPLETE, nSEL15, nSEL25, OR_DC1_L0_0, T_DC0_0, T_DC0_0_a0, T_DC0_0_a1,
       T_DC0_1, T_DC0_1_a0, T_DC1_0, T_DC1_0_a0, T_DC1_0_a1, T_DC1_1, T_DC1_1_a0, T_DC1_1_a1, T_DC1_1_b1_0,
       T_DC1_2, T_DC1_2_a0, T_DC1_2_a1, T_DC2_0_a0, T_DC2_0_a1, T_IMPRIME15_0_a0, T_IMPRIME25_0_a0,
       T_MODE15_0_a0, T_MODE25_0_a0;

  not not_1 (nC2, C2);
  not not_2 (nC1, C1);
  not not_3 (nC0, C0);
  not not_4 (nSEL15, SEL15);
  not not_5 (nSEL25, SEL25);
  not not_6 (nCOMPLETE, COMPLETE);
  D_Flip_Flop FF_C2 (.clk(CLK), .D(DC2), .Q(C2), .preset(1'b0), .reset(Reset));  // open: Qn
  and and_1 (T_DC2_0_a0, nC2, C1);
  and and_2 (T_DC2_0_a1, nC0, COMPLETE);
  and and_3 (T_DC1_0_a0, nC2, nC1);
  and and_4 (T_DC1_0_a1, C0, COMPLETE);
  and and_5 (T_DC1_1_a0, nC2, nC1);
  and and_6 (T_DC1_1_a1, nC0, nSEL15);
  and and_7 (T_DC1_2_a0, nC2, C1);
  and and_8 (T_DC1_2_a1, nC0, nCOMPLETE);
  and and_9 (T_DC0_0_a0, nC2, nC1);
  and and_10 (T_DC0_0_a1, SEL15, nSEL25);
  and and_11 (T_DC0_1_a0, nC2, nC1);
  and and_12 (T_MODE15_0_a0, nC2, nC1);
  and and_13 (T_MODE25_0_a0, nC2, C1);
  and and_14 (T_IMPRIME15_0_a0, nC2, C1);
  and and_15 (T_IMPRIME25_0_a0, C2, nC1);
  D_Flip_Flop FF_C1 (.clk(CLK), .D(DC1), .Q(C1), .preset(1'b0), .reset(Reset));  // open: Qn
  and and_16 (DC2, T_DC2_0_a0, T_DC2_0_a1);
  and and_17 (T_DC1_0, T_DC1_0_a0, T_DC1_0_a1);
  and and_18 (T_DC1_1_b1_0, T_DC1_1_a0, T_DC1_1_a1);
  and and_19 (T_DC1_2, T_DC1_2_a0, T_DC1_2_a1);
  and and_20 (T_DC0_0, T_DC0_0_a0, T_DC0_0_a1);
  and and_21 (T_DC0_1, T_DC0_1_a0, C0);
  and and_22 (MODE15, T_MODE15_0_a0, C0);
  and and_23 (MODE25, T_MODE25_0_a0, nC0);
  and and_24 (IMPRIME15, T_IMPRIME15_0_a0, C0);
  and and_25 (IMPRIME25, T_IMPRIME25_0_a0, nC0);
  and and_26 (T_DC1_1, T_DC1_1_b1_0, SEL25);
  D_Flip_Flop FF_C0 (.clk(CLK), .D(DC0), .Q(C0), .preset(1'b0), .reset(Reset));  // open: Qn
  or or_1 (OR_DC1_L0_0, T_DC1_0, T_DC1_1);
  or or_2 (DC0, T_DC0_0, T_DC0_1);
  or or_3 (DC1, OR_DC1_L0_0, T_DC1_2);

  // Other names for the same wires on the sheet: T_IMPRIME25_0_a1 = nC0; T_MODE25_0_a1 = nC0; T_DC1_1_a2 = SEL25;
  //   T_DC2_0 = DC2; T_IMPRIME15_0 = IMPRIME15; T_IMPRIME25_0 = IMPRIME25; T_MODE15_0 = MODE15; T_DC0_1_a1 = C0;
  //   T_IMPRIME15_0_a1 = C0; T_MODE15_0_a1 = C0; T_MODE25_0 = MODE25

  // Notes on the sheet:
  //   MOORE — Control de ticket
  //   1. Entradas
  //   4. Inversores
  //   Preset=0
  //   5. Logica (siguiente estado y salidas)
  //   DC2
  //   DC1
  //   DC0
  //   MODE15
  //   MODE25
  //   IMPRIME15
  //   IMPRIME25
  //   2. Estado C2 C1 C0
  //   3. Salidas
endmodule

module Mealy (
  input  MODE15,
  input  MODE25,
  input  B20,
  input  B10,
  input  B5,
  input  CLK,
  input  Reset,
  output COMPLETE,
  output C5,
  output C10,
  output C15,
  output P2,
  output P1,
  output P0
);

  wire DP0, DP1, DP2, nB5, nB10, nB20, nMODE15, nMODE25, nP0, nP1, nP2, OR_COMPLETE_L0_0, OR_COMPLETE_L0_1,
       OR_COMPLETE_L0_2, OR_COMPLETE_L0_3, OR_COMPLETE_L0_4, OR_COMPLETE_L0_5, OR_COMPLETE_L0_6,
       OR_COMPLETE_L1_0, OR_COMPLETE_L1_1, OR_COMPLETE_L1_2, OR_COMPLETE_L2_0, OR_COMPLETE_L2_1, OR_DP0_L0_0,
       OR_DP0_L0_1, OR_DP0_L0_2, OR_DP0_L0_3, OR_DP0_L0_4, OR_DP0_L0_5, OR_DP0_L0_6, OR_DP0_L0_7,
       OR_DP0_L1_0, OR_DP0_L1_1, OR_DP0_L1_2, OR_DP0_L1_3, OR_DP0_L2_0, OR_DP0_L2_1, OR_DP1_L0_0,
       OR_DP1_L0_1, OR_DP1_L0_2, OR_DP1_L0_3, OR_DP1_L0_4, OR_DP1_L0_5, OR_DP1_L0_6, OR_DP1_L0_7,
       OR_DP1_L0_8, OR_DP1_L1_0, OR_DP1_L1_1, OR_DP1_L1_2, OR_DP1_L1_3, OR_DP1_L2_0, OR_DP1_L2_1,
       OR_DP1_L3_0, OR_DP2_L0_0, OR_DP2_L0_1, OR_DP2_L0_2, OR_DP2_L0_3, OR_DP2_L0_4, OR_DP2_L0_5,
       OR_DP2_L0_6, OR_DP2_L0_7, OR_DP2_L0_8, OR_DP2_L0_9, OR_DP2_L0_10, OR_DP2_L1_0, OR_DP2_L1_1,
       OR_DP2_L1_2, OR_DP2_L1_3, OR_DP2_L1_4, OR_DP2_L2_0, OR_DP2_L2_1, OR_DP2_L2_2, OR_DP2_L3_0, T_C5_0,
       T_C5_1, T_C10_0, T_C10_1, T_C15_0, T_C15_1, T_COMPLETE_0, T_COMPLETE_0_a0, T_COMPLETE_0_a1,
       T_COMPLETE_0_b1_0, T_COMPLETE_1, T_COMPLETE_1_a0, T_COMPLETE_1_a1, T_COMPLETE_2, T_COMPLETE_2_a0,
       T_COMPLETE_2_a1, T_COMPLETE_2_b1_0, T_COMPLETE_3, T_COMPLETE_3_a0, T_COMPLETE_3_a1, T_COMPLETE_4,
       T_COMPLETE_4_a0, T_COMPLETE_4_a1, T_COMPLETE_5, T_COMPLETE_5_a0, T_COMPLETE_6, T_COMPLETE_6_a0,
       T_COMPLETE_6_a1, T_COMPLETE_6_b1_0, T_COMPLETE_7, T_COMPLETE_7_a0, T_COMPLETE_7_a1, T_COMPLETE_7_b1_0,
       T_COMPLETE_8, T_COMPLETE_8_a0, T_COMPLETE_8_a1, T_COMPLETE_8_b1_0, T_COMPLETE_9, T_COMPLETE_9_a0,
       T_COMPLETE_9_a1, T_COMPLETE_9_b1_0, T_COMPLETE_10, T_COMPLETE_10_a0, T_COMPLETE_11, T_COMPLETE_11_a0,
       T_COMPLETE_11_a1, T_COMPLETE_11_b1_0, T_COMPLETE_12, T_COMPLETE_12_a0, T_COMPLETE_12_a1,
       T_COMPLETE_12_b1_0, T_COMPLETE_13, T_COMPLETE_13_a0, T_COMPLETE_13_a1, T_DP0_0, T_DP0_0_a0,
       T_DP0_0_a1, T_DP0_0_b1_0, T_DP0_1, T_DP0_1_a0, T_DP0_1_a1, T_DP0_1_b1_0, T_DP0_2, T_DP0_2_a0,
       T_DP0_2_a1, T_DP0_3, T_DP0_3_a0, T_DP0_3_a1, T_DP0_3_b1_0, T_DP0_4, T_DP0_4_a0, T_DP0_4_a1,
       T_DP0_4_b1_0, T_DP0_5, T_DP0_5_a0, T_DP0_5_a1, T_DP0_5_b1_0, T_DP0_6, T_DP0_6_a0, T_DP0_6_a1,
       T_DP0_6_b1_0, T_DP0_7, T_DP0_7_a0, T_DP0_7_a1, T_DP0_8, T_DP0_8_a0, T_DP0_8_a1, T_DP0_9, T_DP0_9_a0,
       T_DP0_9_a1, T_DP0_9_b1_0, T_DP0_10, T_DP0_10_a0, T_DP0_10_a1, T_DP0_10_b1_0, T_DP0_11, T_DP0_11_a0,
       T_DP0_11_a1, T_DP0_12, T_DP0_12_a0, T_DP0_12_a1, T_DP0_12_b1_0, T_DP0_13, T_DP0_13_a0, T_DP0_14,
       T_DP0_14_a0, T_DP0_14_a1, T_DP0_14_b1_0, T_DP0_15, T_DP0_15_a0, T_DP0_15_a1, T_DP1_0, T_DP1_0_a0,
       T_DP1_0_a1, T_DP1_0_a2, T_DP1_0_b1_0, T_DP1_1, T_DP1_1_a0, T_DP1_1_a1, T_DP1_1_b1_0, T_DP1_2,
       T_DP1_2_a0, T_DP1_2_a1, T_DP1_2_b1_0, T_DP1_3, T_DP1_3_a0, T_DP1_3_a1, T_DP1_3_a2, T_DP1_3_b1_0,
       T_DP1_4, T_DP1_4_a0, T_DP1_4_a1, T_DP1_5, T_DP1_5_a0, T_DP1_5_a1, T_DP1_5_b1_0, T_DP1_6, T_DP1_6_a0,
       T_DP1_6_a1, T_DP1_6_b1_0, T_DP1_7, T_DP1_7_a0, T_DP1_7_a1, T_DP1_8, T_DP1_8_a0, T_DP1_8_a1,
       T_DP1_8_a2, T_DP1_8_b1_0, T_DP1_9, T_DP1_9_a0, T_DP1_9_a1, T_DP1_9_b1_0, T_DP1_10, T_DP1_10_a0,
       T_DP1_10_a1, T_DP1_10_b1_0, T_DP1_11, T_DP1_11_a0, T_DP1_11_a1, T_DP1_12, T_DP1_12_a0, T_DP1_12_a1,
       T_DP1_12_a2, T_DP1_12_b1_0, T_DP1_13, T_DP1_13_a0, T_DP1_14, T_DP1_14_a0, T_DP1_14_a1, T_DP1_14_b1_0,
       T_DP1_15, T_DP1_15_a0, T_DP1_15_a1, T_DP1_16, T_DP1_16_a0, T_DP1_16_a1, T_DP1_16_a2, T_DP1_16_b1_0,
       T_DP1_17, T_DP1_17_a0, T_DP1_17_a1, T_DP1_17_b1_0, T_DP2_0, T_DP2_0_a0, T_DP2_0_a1, T_DP2_0_b1_0,
       T_DP2_1, T_DP2_1_a0, T_DP2_1_a1, T_DP2_1_b1_0, T_DP2_2, T_DP2_2_a0, T_DP2_2_a1, T_DP2_2_b1_0, T_DP2_3,
       T_DP2_3_a0, T_DP2_3_a1, T_DP2_3_b1_0, T_DP2_4, T_DP2_4_a0, T_DP2_4_a1, T_DP2_4_a2, T_DP2_4_b1_0,
       T_DP2_5, T_DP2_5_a0, T_DP2_5_a1, T_DP2_5_b1_0, T_DP2_6, T_DP2_6_a0, T_DP2_6_a1, T_DP2_6_b1_0, T_DP2_7,
       T_DP2_7_a0, T_DP2_7_a1, T_DP2_7_a2, T_DP2_7_b1_0, T_DP2_8, T_DP2_8_a0, T_DP2_8_a1, T_DP2_9,
       T_DP2_9_a0, T_DP2_9_a1, T_DP2_10, T_DP2_10_a0, T_DP2_10_a1, T_DP2_10_b1_0, T_DP2_11, T_DP2_11_a0,
       T_DP2_11_a1, T_DP2_12, T_DP2_12_a0, T_DP2_12_a1, T_DP2_12_b1_0, T_DP2_13, T_DP2_13_a0, T_DP2_13_a1,
       T_DP2_13_b1_0, T_DP2_14, T_DP2_14_a0, T_DP2_14_a1, T_DP2_15, T_DP2_15_a0, T_DP2_15_a1, T_DP2_15_b1_0,
       T_DP2_16, T_DP2_16_a0, T_DP2_16_a1, T_DP2_16_a2, T_DP2_16_b1_0, T_DP2_17, T_DP2_17_a0, T_DP2_18,
       T_DP2_18_a0, T_DP2_18_a1, T_DP2_18_b1_0, T_DP2_19, T_DP2_19_a0, T_DP2_19_a1, T_DP2_19_a2,
       T_DP2_19_b1_0, T_DP2_20, T_DP2_20_a0, T_DP2_20_a1, T_DP2_21, T_DP2_21_a0, T_DP2_21_a1, T_DP2_21_b1_0;

  not not_1 (nP2, P2);
  not not_2 (nP1, P1);
  not not_3 (nP0, P0);
  not not_4 (nMODE15, MODE15);
  not not_5 (nMODE25, MODE25);
  not not_6 (nB20, B20);
  not not_7 (nB10, B10);
  not not_8 (nB5, B5);
  D_Flip_Flop FF_P2 (.clk(CLK), .D(DP2), .Q(P2), .preset(1'b0), .reset(Reset));  // open: Qn
  and and_1 (T_DP2_0_a0, B20, MODE15);
  and and_2 (T_DP2_0_a1, nP0, nP1);
  and and_3 (T_DP2_1_a0, B10, nB20);
  and and_4 (T_DP2_1_a1, MODE25, P1);
  and and_5 (T_DP2_2_a0, B20, MODE25);
  and and_6 (T_DP2_2_a1, nP0, nP1);
  and and_7 (T_DP2_3_a0, B10, nB20);
  and and_8 (T_DP2_3_a1, MODE15, P1);
  and and_9 (T_DP2_4_a0, B5, nB20);
  and and_10 (T_DP2_4_a1, MODE25, P0);
  and and_11 (T_DP2_4_a2, P1, nP2);
  and and_12 (T_DP2_5_a0, nB10, B20);
  and and_13 (T_DP2_5_a1, MODE15, nP1);
  and and_14 (T_DP2_6_a0, nB10, B20);
  and and_15 (T_DP2_6_a1, MODE25, nP1);
  and and_16 (T_DP2_7_a0, B5, nB20);
  and and_17 (T_DP2_7_a1, MODE15, P0);
  and and_18 (T_DP2_7_a2, P1, nP2);
  and and_19 (T_DP2_8_a0, nB5, nB10);
  and and_20 (T_DP2_8_a1, nB20, P2);
  and and_21 (T_DP2_9_a0, nB10, nB20);
  and and_22 (T_DP2_9_a1, nP0, P2);
  and and_23 (T_DP2_10_a0, nB5, nB10);
  and and_24 (T_DP2_10_a1, B20, MODE15);
  and and_25 (T_DP2_11_a0, nB5, nB20);
  and and_26 (T_DP2_11_a1, nP1, P2);
  and and_27 (T_DP2_12_a0, nB5, nB10);
  and and_28 (T_DP2_12_a1, B20, MODE25);
  and and_29 (T_DP2_13_a0, nB10, B20);
  and and_30 (T_DP2_13_a1, MODE15, nP0);
  and and_31 (T_DP2_14_a0, nB20, nP0);
  and and_32 (T_DP2_14_a1, nP1, P2);
  and and_33 (T_DP2_15_a0, nB10, B20);
  and and_34 (T_DP2_15_a1, MODE25, nP0);
  and and_35 (T_DP2_16_a0, B5, B10);
  and and_36 (T_DP2_16_a1, nB20, MODE15);
  and and_37 (T_DP2_16_a2, P0, nP2);
  and and_38 (T_DP2_17_a0, nMODE25, nMODE15);
  and and_39 (T_DP2_18_a0, nB5, B20);
  and and_40 (T_DP2_18_a1, MODE15, nP1);
  and and_41 (T_DP2_19_a0, B5, B10);
  and and_42 (T_DP2_19_a1, nB20, MODE25);
  and and_43 (T_DP2_19_a2, P0, nP2);
  and and_44 (T_DP2_20_a0, nB10, nB20);
  and and_45 (T_DP2_20_a1, nP1, P2);
  and and_46 (T_DP2_21_a0, nB5, B20);
  and and_47 (T_DP2_21_a1, MODE25, nP1);
  and and_48 (T_DP1_0_a0, B5, nB10);
  and and_49 (T_DP1_0_a1, nB20, MODE15);
  and and_50 (T_DP1_0_a2, P0, nP1);
  and and_51 (T_DP1_1_a0, B10, MODE25);
  and and_52 (T_DP1_1_a1, nP0, nP1);
  and and_53 (T_DP1_2_a0, nB5, B10);
  and and_54 (T_DP1_2_a1, nB20, MODE15);
  and and_55 (T_DP1_3_a0, B5, nB10);
  and and_56 (T_DP1_3_a1, MODE25, P0);
  and and_57 (T_DP1_3_a2, nP1, nP2);
  and and_58 (T_DP1_4_a0, nB5, nB10);
  and and_59 (T_DP1_4_a1, nB20, P1);
  and and_60 (T_DP1_5_a0, nB5, B10);
  and and_61 (T_DP1_5_a1, MODE25, nP1);
  and and_62 (T_DP1_6_a0, B10, MODE15);
  and and_63 (T_DP1_6_a1, nP0, nP1);
  and and_64 (T_DP1_7_a0, nB10, nB20);
  and and_65 (T_DP1_7_a1, nP0, P1);
  and and_66 (T_DP1_8_a0, B5, nB10);
  and and_67 (T_DP1_8_a1, MODE15, P0);
  and and_68 (T_DP1_8_a2, nP1, nP2);
  and and_69 (T_DP1_9_a0, B10, nB20);
  and and_70 (T_DP1_9_a1, MODE25, nP0);
  and and_71 (T_DP1_10_a0, nB5, B10);
  and and_72 (T_DP1_10_a1, MODE15, nP1);
  and and_73 (T_DP1_11_a0, nB10, nP0);
  and and_74 (T_DP1_11_a1, P1, nP2);
  and and_75 (T_DP1_12_a0, B5, nB10);
  and and_76 (T_DP1_12_a1, nB20, MODE25);
  and and_77 (T_DP1_12_a2, P0, nP1);
  and and_78 (T_DP1_13_a0, nMODE25, nMODE15);
  and and_79 (T_DP1_14_a0, B10, nB20);
  and and_80 (T_DP1_14_a1, MODE15, nP0);
  and and_81 (T_DP1_15_a0, nB5, nB10);
  and and_82 (T_DP1_15_a1, P1, nP2);
  and and_83 (T_DP1_16_a0, B5, B10);
  and and_84 (T_DP1_16_a1, nB20, P0);
  and and_85 (T_DP1_16_a2, P1, nP2);
  and and_86 (T_DP1_17_a0, nB5, B10);
  and and_87 (T_DP1_17_a1, nB20, MODE25);
  and and_88 (T_DP0_0_a0, B5, nB10);
  and and_89 (T_DP0_0_a1, MODE25, nP0);
  and and_90 (T_DP0_1_a0, B5, nB10);
  and and_91 (T_DP0_1_a1, nB20, MODE15);
  and and_92 (T_DP0_2_a0, nB5, P0);
  and and_93 (T_DP0_2_a1, nP1, nP2);
  and and_94 (T_DP0_3_a0, B5, MODE25);
  and and_95 (T_DP0_3_a1, nP0, nP1);
  and and_96 (T_DP0_4_a0, B5, nB10);
  and and_97 (T_DP0_4_a1, nB20, MODE25);
  and and_98 (T_DP0_5_a0, B5, nB20);
  and and_99 (T_DP0_5_a1, MODE15, nP0);
  and and_100 (T_DP0_6_a0, B5, nB20);
  and and_101 (T_DP0_6_a1, MODE15, nP0);
  and and_102 (T_DP0_7_a0, nB5, nB10);
  and and_103 (T_DP0_7_a1, nB20, P0);
  and and_104 (T_DP0_8_a0, nB5, nB20);
  and and_105 (T_DP0_8_a1, P0, nP2);
  and and_106 (T_DP0_9_a0, B5, nB10);
  and and_107 (T_DP0_9_a1, MODE15, nP0);
  and and_108 (T_DP0_10_a0, B5, nB20);
  and and_109 (T_DP0_10_a1, MODE25, nP0);
  and and_110 (T_DP0_11_a0, nB5, nB20);
  and and_111 (T_DP0_11_a1, P0, nP1);
  and and_112 (T_DP0_12_a0, B5, nB20);
  and and_113 (T_DP0_12_a1, MODE25, nP0);
  and and_114 (T_DP0_13_a0, nMODE25, nMODE15);
  and and_115 (T_DP0_14_a0, B5, MODE15);
  and and_116 (T_DP0_14_a1, nP0, nP1);
  and and_117 (T_DP0_15_a0, nB5, nB10);
  and and_118 (T_DP0_15_a1, P0, nP2);
  and and_119 (T_COMPLETE_0_a0, B5, B20);
  and and_120 (T_COMPLETE_0_a1, MODE25, P0);
  and and_121 (T_COMPLETE_1_a0, B10, MODE25);
  and and_122 (T_COMPLETE_1_a1, P1, P2);
  and and_123 (T_COMPLETE_2_a0, B5, B10);
  and and_124 (T_COMPLETE_2_a1, MODE25, P0);
  and and_125 (T_COMPLETE_3_a0, B10, B20);
  and and_126 (T_COMPLETE_3_a1, MODE25, P1);
  and and_127 (T_COMPLETE_4_a0, B10, MODE15);
  and and_128 (T_COMPLETE_4_a1, P1, P2);
  and and_129 (T_COMPLETE_5_a0, B20, MODE15);
  and and_130 (T_COMPLETE_6_a0, B5, B20);
  and and_131 (T_COMPLETE_6_a1, MODE15, P0);
  and and_132 (T_COMPLETE_7_a0, B5, B10);
  and and_133 (T_COMPLETE_7_a1, B20, MODE15);
  and and_134 (T_COMPLETE_8_a0, B5, B10);
  and and_135 (T_COMPLETE_8_a1, MODE15, P0);
  and and_136 (T_COMPLETE_9_a0, B5, MODE25);
  and and_137 (T_COMPLETE_9_a1, P0, P1);
  and and_138 (T_COMPLETE_10_a0, B20, MODE25);
  and and_139 (T_COMPLETE_11_a0, B5, B10);
  and and_140 (T_COMPLETE_11_a1, B20, MODE25);
  and and_141 (T_COMPLETE_12_a0, B5, MODE15);
  and and_142 (T_COMPLETE_12_a1, P0, P1);
  and and_143 (T_COMPLETE_13_a0, B10, B20);
  and and_144 (T_COMPLETE_13_a1, MODE15, P1);
  and and_145 (T_C5_0, B5, MODE25);
  and and_146 (T_C5_1, B5, MODE15);
  and and_147 (T_C10_0, B10, MODE15);
  and and_148 (T_C10_1, B10, MODE25);
  and and_149 (T_C15_0, B20, MODE25);
  and and_150 (T_C15_1, B20, MODE15);
  D_Flip_Flop FF_P1 (.clk(CLK), .D(DP1), .Q(P1), .preset(1'b0), .reset(Reset));  // open: Qn
  and and_151 (T_DP2_0_b1_0, T_DP2_0_a0, T_DP2_0_a1);
  and and_152 (T_DP2_1_b1_0, T_DP2_1_a0, T_DP2_1_a1);
  and and_153 (T_DP2_2_b1_0, T_DP2_2_a0, T_DP2_2_a1);
  and and_154 (T_DP2_3_b1_0, T_DP2_3_a0, T_DP2_3_a1);
  and and_155 (T_DP2_4_b1_0, T_DP2_4_a0, T_DP2_4_a1);
  and and_156 (T_DP2_5_b1_0, T_DP2_5_a0, T_DP2_5_a1);
  and and_157 (T_DP2_6_b1_0, T_DP2_6_a0, T_DP2_6_a1);
  and and_158 (T_DP2_7_b1_0, T_DP2_7_a0, T_DP2_7_a1);
  and and_159 (T_DP2_8, T_DP2_8_a0, T_DP2_8_a1);
  and and_160 (T_DP2_9, T_DP2_9_a0, T_DP2_9_a1);
  and and_161 (T_DP2_10_b1_0, T_DP2_10_a0, T_DP2_10_a1);
  and and_162 (T_DP2_11, T_DP2_11_a0, T_DP2_11_a1);
  and and_163 (T_DP2_12_b1_0, T_DP2_12_a0, T_DP2_12_a1);
  and and_164 (T_DP2_13_b1_0, T_DP2_13_a0, T_DP2_13_a1);
  and and_165 (T_DP2_14, T_DP2_14_a0, T_DP2_14_a1);
  and and_166 (T_DP2_15_b1_0, T_DP2_15_a0, T_DP2_15_a1);
  and and_167 (T_DP2_16_b1_0, T_DP2_16_a0, T_DP2_16_a1);
  and and_168 (T_DP2_17, T_DP2_17_a0, P2);
  and and_169 (T_DP2_18_b1_0, T_DP2_18_a0, T_DP2_18_a1);
  and and_170 (T_DP2_19_b1_0, T_DP2_19_a0, T_DP2_19_a1);
  and and_171 (T_DP2_20, T_DP2_20_a0, T_DP2_20_a1);
  and and_172 (T_DP2_21_b1_0, T_DP2_21_a0, T_DP2_21_a1);
  and and_173 (T_DP1_0_b1_0, T_DP1_0_a0, T_DP1_0_a1);
  and and_174 (T_DP1_1_b1_0, T_DP1_1_a0, T_DP1_1_a1);
  and and_175 (T_DP1_2_b1_0, T_DP1_2_a0, T_DP1_2_a1);
  and and_176 (T_DP1_3_b1_0, T_DP1_3_a0, T_DP1_3_a1);
  and and_177 (T_DP1_4, T_DP1_4_a0, T_DP1_4_a1);
  and and_178 (T_DP1_5_b1_0, T_DP1_5_a0, T_DP1_5_a1);
  and and_179 (T_DP1_6_b1_0, T_DP1_6_a0, T_DP1_6_a1);
  and and_180 (T_DP1_7, T_DP1_7_a0, T_DP1_7_a1);
  and and_181 (T_DP1_8_b1_0, T_DP1_8_a0, T_DP1_8_a1);
  and and_182 (T_DP1_9_b1_0, T_DP1_9_a0, T_DP1_9_a1);
  and and_183 (T_DP1_10_b1_0, T_DP1_10_a0, T_DP1_10_a1);
  and and_184 (T_DP1_11, T_DP1_11_a0, T_DP1_11_a1);
  and and_185 (T_DP1_12_b1_0, T_DP1_12_a0, T_DP1_12_a1);
  and and_186 (T_DP1_13, T_DP1_13_a0, P1);
  and and_187 (T_DP1_14_b1_0, T_DP1_14_a0, T_DP1_14_a1);
  and and_188 (T_DP1_15, T_DP1_15_a0, T_DP1_15_a1);
  and and_189 (T_DP1_16_b1_0, T_DP1_16_a0, T_DP1_16_a1);
  and and_190 (T_DP1_17_b1_0, T_DP1_17_a0, T_DP1_17_a1);
  and and_191 (T_DP0_0_b1_0, T_DP0_0_a0, T_DP0_0_a1);
  and and_192 (T_DP0_1_b1_0, T_DP0_1_a0, T_DP0_1_a1);
  and and_193 (T_DP0_2, T_DP0_2_a0, T_DP0_2_a1);
  and and_194 (T_DP0_3_b1_0, T_DP0_3_a0, T_DP0_3_a1);
  and and_195 (T_DP0_4_b1_0, T_DP0_4_a0, T_DP0_4_a1);
  and and_196 (T_DP0_5_b1_0, T_DP0_5_a0, T_DP0_5_a1);
  and and_197 (T_DP0_6_b1_0, T_DP0_6_a0, T_DP0_6_a1);
  and and_198 (T_DP0_7, T_DP0_7_a0, T_DP0_7_a1);
  and and_199 (T_DP0_8, T_DP0_8_a0, T_DP0_8_a1);
  and and_200 (T_DP0_9_b1_0, T_DP0_9_a0, T_DP0_9_a1);
  and and_201 (T_DP0_10_b1_0, T_DP0_10_a0, T_DP0_10_a1);
  and and_202 (T_DP0_11, T_DP0_11_a0, T_DP0_11_a1);
  and and_203 (T_DP0_12_b1_0, T_DP0_12_a0, T_DP0_12_a1);
  and and_204 (T_DP0_13, T_DP0_13_a0, P0);
  and and_205 (T_DP0_14_b1_0, T_DP0_14_a0, T_DP0_14_a1);
  and and_206 (T_DP0_15, T_DP0_15_a0, T_DP0_15_a1);
  and and_207 (T_COMPLETE_0_b1_0, T_COMPLETE_0_a0, T_COMPLETE_0_a1);
  and and_208 (T_COMPLETE_1, T_COMPLETE_1_a0, T_COMPLETE_1_a1);
  and and_209 (T_COMPLETE_2_b1_0, T_COMPLETE_2_a0, T_COMPLETE_2_a1);
  and and_210 (T_COMPLETE_3, T_COMPLETE_3_a0, T_COMPLETE_3_a1);
  and and_211 (T_COMPLETE_4, T_COMPLETE_4_a0, T_COMPLETE_4_a1);
  and and_212 (T_COMPLETE_5, T_COMPLETE_5_a0, P2);
  and and_213 (T_COMPLETE_6_b1_0, T_COMPLETE_6_a0, T_COMPLETE_6_a1);
  and and_214 (T_COMPLETE_7_b1_0, T_COMPLETE_7_a0, T_COMPLETE_7_a1);
  and and_215 (T_COMPLETE_8_b1_0, T_COMPLETE_8_a0, T_COMPLETE_8_a1);
  and and_216 (T_COMPLETE_9_b1_0, T_COMPLETE_9_a0, T_COMPLETE_9_a1);
  and and_217 (T_COMPLETE_10, T_COMPLETE_10_a0, P2);
  and and_218 (T_COMPLETE_11_b1_0, T_COMPLETE_11_a0, T_COMPLETE_11_a1);
  and and_219 (T_COMPLETE_12_b1_0, T_COMPLETE_12_a0, T_COMPLETE_12_a1);
  and and_220 (T_COMPLETE_13, T_COMPLETE_13_a0, T_COMPLETE_13_a1);
  and and_221 (T_DP2_0, T_DP2_0_b1_0, nP2);
  and and_222 (T_DP2_1, T_DP2_1_b1_0, nP2);
  and and_223 (T_DP2_2, T_DP2_2_b1_0, nP2);
  and and_224 (T_DP2_3, T_DP2_3_b1_0, nP2);
  and and_225 (T_DP2_4, T_DP2_4_b1_0, T_DP2_4_a2);
  and and_226 (T_DP2_5, T_DP2_5_b1_0, nP2);
  and and_227 (T_DP2_6, T_DP2_6_b1_0, nP2);
  and and_228 (T_DP2_7, T_DP2_7_b1_0, T_DP2_7_a2);
  and and_229 (T_DP2_10, T_DP2_10_b1_0, nP2);
  and and_230 (T_DP2_12, T_DP2_12_b1_0, nP2);
  and and_231 (T_DP2_13, T_DP2_13_b1_0, nP2);
  and and_232 (T_DP2_15, T_DP2_15_b1_0, nP2);
  and and_233 (T_DP2_16, T_DP2_16_b1_0, T_DP2_16_a2);
  and and_234 (T_DP2_18, T_DP2_18_b1_0, nP2);
  and and_235 (T_DP2_19, T_DP2_19_b1_0, T_DP2_19_a2);
  and and_236 (T_DP2_21, T_DP2_21_b1_0, nP2);
  and and_237 (T_DP1_0, T_DP1_0_b1_0, T_DP1_0_a2);
  and and_238 (T_DP1_1, T_DP1_1_b1_0, nP2);
  and and_239 (T_DP1_2, T_DP1_2_b1_0, nP1);
  and and_240 (T_DP1_3, T_DP1_3_b1_0, T_DP1_3_a2);
  and and_241 (T_DP1_5, T_DP1_5_b1_0, nP2);
  and and_242 (T_DP1_6, T_DP1_6_b1_0, nP2);
  and and_243 (T_DP1_8, T_DP1_8_b1_0, T_DP1_8_a2);
  and and_244 (T_DP1_9, T_DP1_9_b1_0, nP1);
  and and_245 (T_DP1_10, T_DP1_10_b1_0, nP2);
  and and_246 (T_DP1_12, T_DP1_12_b1_0, T_DP1_12_a2);
  and and_247 (T_DP1_14, T_DP1_14_b1_0, nP1);
  and and_248 (T_DP1_16, T_DP1_16_b1_0, T_DP1_16_a2);
  and and_249 (T_DP1_17, T_DP1_17_b1_0, nP1);
  and and_250 (T_DP0_0, T_DP0_0_b1_0, nP2);
  and and_251 (T_DP0_1, T_DP0_1_b1_0, nP0);
  and and_252 (T_DP0_3, T_DP0_3_b1_0, nP2);
  and and_253 (T_DP0_4, T_DP0_4_b1_0, nP0);
  and and_254 (T_DP0_5, T_DP0_5_b1_0, nP2);
  and and_255 (T_DP0_6, T_DP0_6_b1_0, nP1);
  and and_256 (T_DP0_9, T_DP0_9_b1_0, nP2);
  and and_257 (T_DP0_10, T_DP0_10_b1_0, nP2);
  and and_258 (T_DP0_12, T_DP0_12_b1_0, nP1);
  and and_259 (T_DP0_14, T_DP0_14_b1_0, nP2);
  and and_260 (T_COMPLETE_0, T_COMPLETE_0_b1_0, P1);
  and and_261 (T_COMPLETE_2, T_COMPLETE_2_b1_0, P2);
  and and_262 (T_COMPLETE_6, T_COMPLETE_6_b1_0, P1);
  and and_263 (T_COMPLETE_7, T_COMPLETE_7_b1_0, P0);
  and and_264 (T_COMPLETE_8, T_COMPLETE_8_b1_0, P2);
  and and_265 (T_COMPLETE_9, T_COMPLETE_9_b1_0, P2);
  and and_266 (T_COMPLETE_11, T_COMPLETE_11_b1_0, P0);
  and and_267 (T_COMPLETE_12, T_COMPLETE_12_b1_0, P2);
  D_Flip_Flop FF_P0 (.clk(CLK), .D(DP0), .Q(P0), .preset(1'b0), .reset(Reset));  // open: Qn
  or or_1 (OR_DP2_L0_0, T_DP2_0, T_DP2_1);
  or or_2 (OR_DP2_L0_1, T_DP2_2, T_DP2_3);
  or or_3 (OR_DP2_L0_2, T_DP2_4, T_DP2_5);
  or or_4 (OR_DP2_L0_3, T_DP2_6, T_DP2_7);
  or or_5 (OR_DP2_L0_4, T_DP2_8, T_DP2_9);
  or or_6 (OR_DP2_L0_5, T_DP2_10, T_DP2_11);
  or or_7 (OR_DP2_L0_6, T_DP2_12, T_DP2_13);
  or or_8 (OR_DP2_L0_7, T_DP2_14, T_DP2_15);
  or or_9 (OR_DP2_L0_8, T_DP2_16, T_DP2_17);
  or or_10 (OR_DP2_L0_9, T_DP2_18, T_DP2_19);
  or or_11 (OR_DP2_L0_10, T_DP2_20, T_DP2_21);
  or or_12 (OR_DP1_L0_0, T_DP1_0, T_DP1_1);
  or or_13 (OR_DP1_L0_1, T_DP1_2, T_DP1_3);
  or or_14 (OR_DP1_L0_2, T_DP1_4, T_DP1_5);
  or or_15 (OR_DP1_L0_3, T_DP1_6, T_DP1_7);
  or or_16 (OR_DP1_L0_4, T_DP1_8, T_DP1_9);
  or or_17 (OR_DP1_L0_5, T_DP1_10, T_DP1_11);
  or or_18 (OR_DP1_L0_6, T_DP1_12, T_DP1_13);
  or or_19 (OR_DP1_L0_7, T_DP1_14, T_DP1_15);
  or or_20 (OR_DP1_L0_8, T_DP1_16, T_DP1_17);
  or or_21 (OR_DP0_L0_0, T_DP0_0, T_DP0_1);
  or or_22 (OR_DP0_L0_1, T_DP0_2, T_DP0_3);
  or or_23 (OR_DP0_L0_2, T_DP0_4, T_DP0_5);
  or or_24 (OR_DP0_L0_3, T_DP0_6, T_DP0_7);
  or or_25 (OR_DP0_L0_4, T_DP0_8, T_DP0_9);
  or or_26 (OR_DP0_L0_5, T_DP0_10, T_DP0_11);
  or or_27 (OR_DP0_L0_6, T_DP0_12, T_DP0_13);
  or or_28 (OR_DP0_L0_7, T_DP0_14, T_DP0_15);
  or or_29 (OR_COMPLETE_L0_0, T_COMPLETE_0, T_COMPLETE_1);
  or or_30 (OR_COMPLETE_L0_1, T_COMPLETE_2, T_COMPLETE_3);
  or or_31 (OR_COMPLETE_L0_2, T_COMPLETE_4, T_COMPLETE_5);
  or or_32 (OR_COMPLETE_L0_3, T_COMPLETE_6, T_COMPLETE_7);
  or or_33 (OR_COMPLETE_L0_4, T_COMPLETE_8, T_COMPLETE_9);
  or or_34 (OR_COMPLETE_L0_5, T_COMPLETE_10, T_COMPLETE_11);
  or or_35 (OR_COMPLETE_L0_6, T_COMPLETE_12, T_COMPLETE_13);
  or or_36 (C5, T_C5_0, T_C5_1);
  or or_37 (C10, T_C10_0, T_C10_1);
  or or_38 (C15, T_C15_0, T_C15_1);
  or or_39 (OR_DP2_L1_0, OR_DP2_L0_0, OR_DP2_L0_1);
  or or_40 (OR_DP2_L1_1, OR_DP2_L0_2, OR_DP2_L0_3);
  or or_41 (OR_DP2_L1_2, OR_DP2_L0_4, OR_DP2_L0_5);
  or or_42 (OR_DP2_L1_3, OR_DP2_L0_6, OR_DP2_L0_7);
  or or_43 (OR_DP2_L1_4, OR_DP2_L0_8, OR_DP2_L0_9);
  or or_44 (OR_DP1_L1_0, OR_DP1_L0_0, OR_DP1_L0_1);
  or or_45 (OR_DP1_L1_1, OR_DP1_L0_2, OR_DP1_L0_3);
  or or_46 (OR_DP1_L1_2, OR_DP1_L0_4, OR_DP1_L0_5);
  or or_47 (OR_DP1_L1_3, OR_DP1_L0_6, OR_DP1_L0_7);
  or or_48 (OR_DP0_L1_0, OR_DP0_L0_0, OR_DP0_L0_1);
  or or_49 (OR_DP0_L1_1, OR_DP0_L0_2, OR_DP0_L0_3);
  or or_50 (OR_DP0_L1_2, OR_DP0_L0_4, OR_DP0_L0_5);
  or or_51 (OR_DP0_L1_3, OR_DP0_L0_6, OR_DP0_L0_7);
  or or_52 (OR_COMPLETE_L1_0, OR_COMPLETE_L0_0, OR_COMPLETE_L0_1);
  or or_53 (OR_COMPLETE_L1_1, OR_COMPLETE_L0_2, OR_COMPLETE_L0_3);
  or or_54 (OR_COMPLETE_L1_2, OR_COMPLETE_L0_4, OR_COMPLETE_L0_5);
  or or_55 (OR_DP2_L2_0, OR_DP2_L1_0, OR_DP2_L1_1);
  or or_56 (OR_DP2_L2_1, OR_DP2_L1_2, OR_DP2_L1_3);
  or or_57 (OR_DP2_L2_2, OR_DP2_L1_4, OR_DP2_L0_10);
  or or_58 (OR_DP1_L2_0, OR_DP1_L1_0, OR_DP1_L1_1);
  or or_59 (OR_DP1_L2_1, OR_DP1_L1_2, OR_DP1_L1_3);
  or or_60 (OR_DP0_L2_0, OR_DP0_L1_0, OR_DP0_L1_1);
  or or_61 (OR_DP0_L2_1, OR_DP0_L1_2, OR_DP0_L1_3);
  or or_62 (OR_COMPLETE_L2_0, OR_COMPLETE_L1_0, OR_COMPLETE_L1_1);
  or or_63 (OR_COMPLETE_L2_1, OR_COMPLETE_L1_2, OR_COMPLETE_L0_6);
  or or_64 (OR_DP2_L3_0, OR_DP2_L2_0, OR_DP2_L2_1);
  or or_65 (OR_DP1_L3_0, OR_DP1_L2_0, OR_DP1_L2_1);
  or or_66 (DP0, OR_DP0_L2_0, OR_DP0_L2_1);
  or or_67 (COMPLETE, OR_COMPLETE_L2_0, OR_COMPLETE_L2_1);
  or or_68 (DP2, OR_DP2_L3_0, OR_DP2_L2_2);
  or or_69 (DP1, OR_DP1_L3_0, OR_DP1_L0_8);

  // Other names for the same wires on the sheet: T_DP0_1_a2 = nP0; T_DP0_4_a2 = nP0; T_DP0_6_a2 = nP1;
  //   T_DP0_12_a2 = nP1; T_DP1_2_a2 = nP1; T_DP1_9_a2 = nP1; T_DP1_14_a2 = nP1; T_DP1_17_a2 = nP1; T_DP0_0_a2 = nP2;
  //   T_DP0_3_a2 = nP2; T_DP0_5_a2 = nP2; T_DP0_9_a2 = nP2; T_DP0_10_a2 = nP2; T_DP0_14_a2 = nP2; T_DP1_1_a2 = nP2;
  //   T_DP1_5_a2 = nP2; T_DP1_6_a2 = nP2; T_DP1_10_a2 = nP2; T_DP2_0_a2 = nP2; T_DP2_1_a2 = nP2; T_DP2_2_a2 = nP2;
  //   T_DP2_3_a2 = nP2; T_DP2_5_a2 = nP2; T_DP2_6_a2 = nP2; T_DP2_10_a2 = nP2; T_DP2_12_a2 = nP2; T_DP2_13_a2 = nP2;
  //   T_DP2_15_a2 = nP2; T_DP2_18_a2 = nP2; T_DP2_21_a2 = nP2; T_C5_0_a0 = T_C5_0; T_C5_1_a0 = T_C5_1;
  //   T_C10_0_a0 = T_C10_0; T_C10_1_a0 = T_C10_1; T_C15_0_a0 = T_C15_0; T_C15_1_a0 = T_C15_1; T_COMPLETE_7_a2 = P0;
  //   T_COMPLETE_11_a2 = P0; T_DP0_13_a1 = P0; T_COMPLETE_0_a2 = P1; T_COMPLETE_6_a2 = P1; T_DP1_13_a1 = P1;
  //   T_COMPLETE_2_a2 = P2; T_COMPLETE_5_a1 = P2; T_COMPLETE_8_a2 = P2; T_COMPLETE_9_a2 = P2; T_COMPLETE_10_a1 = P2;
  //   T_COMPLETE_12_a2 = P2; T_DP2_17_a1 = P2

  // Notes on the sheet:
  //   MEALY — Pago (total 40)
  //   1. Entradas
  //   4. Inversores
  //   Preset=0
  //   5. Logica (acumulacion / COMPLETE)
  //   DP2
  //   DP1
  //   DP0
  //   COMPLETE
  //   C5
  //   C10
  //   C15
  //   2. Estado P2 P1 P0
  //   3. Salidas
endmodule

module main (
  input  SEL15,
  input  SEL25,
  input  B20,
  input  B10,
  input  B5,
  input  Reset,
  output MODE15,
  output MODE25,
  output IMPRIME15,
  output IMPRIME25,
  output C2,
  output C1,
  output C0,
  output COMPLETE,
  output C5,
  output C10,
  output C15,
  output P2,
  output P1,
  output P0
);

  wire CLK;

  Clock u_CLK (.out(CLK));
  Moore moore_1 (
    .SEL15(SEL15), .SEL25(SEL25), .COMPLETE(COMPLETE), .CLK(CLK), .Reset(Reset), .MODE15(MODE15),
    .MODE25(MODE25), .IMPRIME15(IMPRIME15), .IMPRIME25(IMPRIME25), .C2(C2), .C1(C1), .C0(C0));
  // Mealy mealy_1: pin names not known; wires that end beside it: MODE15, MODE25, B20, B10, B5, CLK, Reset, COMPLETE, C5, C10, C15, P2, P1, P0
  LED led_1 (.in(MODE15));
  LED led_2 (.in(MODE25));
  LED led_3 (.in(IMPRIME15));
  LED led_4 (.in(IMPRIME25));
  LED led_5 (.in(C2));
  LED led_6 (.in(C1));
  LED led_7 (.in(C0));
  LED led_8 (.in(COMPLETE));
  LED led_9 (.in(C5));
  LED led_10 (.in(C10));
  LED led_11 (.in(C15));
  LED led_12 (.in(P2));
  LED led_13 (.in(P1));
  LED led_14 (.in(P0));

  // Notes on the sheet:
  //   MAIN — Sistema unificado
  //   Controles
  //   Bloque Moore (ticket)
  //   Bloque Mealy (pago total 40)
  //   LEDs Moore
  //   LEDs Mealy
endmodule
